// Logisim project cpu.circ as structural Verilog: 5 circuits, main circuit main
module main (
  input  Reset,
  output [7:0] Prog__Count,
  output Reg_Write,
  output [15:0] Instruction,
  output [1:0] Imm_Encoding,
  output [15:0] rs1_Data,
  output Use_Imm,
  output [6:0] ALU_CMD,
  output [15:0] rs2_Data,
  output RAM_Write,
  output [15:0] Immediate,
  output [1:0] Reg_Write_Select,
  output [15:0] ALU_Out,
  output [15:0] RAM_out,
  output [15:0] Reg_Write_Data
);

  wire clock_1_out;
  wire [7:0] adder_1_out;
  wire [15:0] multiplexer_1_out;

  Register register_1 (.D(adder_1_out), .Q(Prog__Count), .clk(clock_1_out), .clr(Reset));  // open: en
  Adder adder_1 (.a(Prog__Count), .b(8'h1), .out(adder_1_out));  // open: cin, cout
  ROM #(.dataWidth(16)) rom_1 (.addr(Prog__Count), .data(Instruction));  // open: sel
  Control control_1 (
    .Inst_In(Instruction), .Reg_Write(Reg_Write), .Imm__Encoding(Imm_Encoding), .Imm(Use_Imm),
    .ALU_Operation(ALU_CMD), .Ram_Write(RAM_Write), .Reg_Write_Data(Reg_Write_Select));
  Clock clock_1 (.out(clock_1_out));
  Registers registers_1 (
    .rs1_Sele(Instruction[10:8]), .rs2_Sele(Instruction[13:11]), .Clear(Reset), .Write(Reg_Write),
    .rs0_Sele(Instruction[4:2]), .Write_Input(Reg_Write_Data), .Clock(clock_1_out), .rs1_Data(rs1_Data),
    .rs2_Data(rs2_Data));
  Imm__Proc imm_proc_1 (
    .Immediate_Input(Instruction[15:2]), .Immediate_Output(Immediate), .Immediate_Encoding(Imm_Encoding));
  ALU alu_1 (.IN_1(rs1_Data), .IN_2(multiplexer_1_out), .Out(ALU_Out), .Operation(ALU_CMD));
  Multiplexer #(.width(16), .enable("false")) multiplexer_1 (
    .in0(rs2_Data), .in1(Immediate), .out(multiplexer_1_out), .sel(Use_Imm));
  RAM #(.addrWidth(16), .dataWidth(16), .bus("separate")) ram_1 (
    .addr(ALU_Out), .din(rs2_Data), .data(RAM_out), .str(RAM_Write), .clk(clock_1_out), .clr(Reset));  // open: sel, ld
  Multiplexer #(.select(2), .width(16), .enable("false")) multiplexer_2 (
    .in0(ALU_Out), .in2(Immediate), .in3(RAM_out), .out(Reg_Write_Data), .sel(Reg_Write_Select));  // open: in1

  // Other names for the same wires on the sheet: ALU[15:0] = ALU_Out; c0 = Reg_Write; c1[1:0] = Imm_Encoding;
  //   c2 = Use_Imm; c3[6:0] = ALU_CMD; c4 = RAM_Write; c5[1:0] = Reg_Write_Select; Imm[15:0] = Immediate;
  //   MC[15:0] = Instruction; PC[7:0] = Prog__Count; RAM[15:0] = RAM_out; RegW[15:0] = Reg_Write_Data;
  //   rs1[15:0] = rs1_Data; rs2[15:0] = rs2_Data

  // Notes on the sheet:
  //   contents of rom_1 (hex, n*v repeats v):
  //   2805 1809 100d c811 21f4 1af8 22fc 19f0
  //   ALU
endmodule

module Control (
  input  [15:0] Inst_In,
  output Reg_Write,
  output Imm,
  output Ram_Write,
  output [1:0] Reg_Write_Data,
  output [6:0] ALU_Operation,
  output [1:0] Imm__Encoding
);

  wire [0:0] multiplexer_4_out;

  Multiplexer #(.select(2), .enable("false")) multiplexer_1 (
    .in0(1'b1), .in1(1'b1), .in2(1'b0), .in3(1'b1), .out(Reg_Write), .sel(Inst_In[1:0]));
  Multiplexer #(.select(2), .enable("false")) multiplexer_2 (
    .in0(1'b0), .in1(1'b1), .in2(1'b1), .in3(1'b1), .out(Imm), .sel(Inst_In[1:0]));
  Multiplexer #(.select(2), .enable("false")) multiplexer_3 (
    .in0(1'b0), .in1(1'b0), .in2(1'b1), .in3(1'b0), .out(Ram_Write), .sel(Inst_In[1:0]));
  Multiplexer #(.select(3), .enable("false")) multiplexer_4 (
    .in0(1'b0), .in1(1'b0), .in2(1'b0), .in3(1'b0), .in4(1'b0), .in5(1'b0), .in6(1'b1), .in7(1'b1),
    .out(multiplexer_4_out[0]), .sel(Inst_In[7:5]));
  Multiplexer #(.select(3), .width(2), .enable("false")) multiplexer_5 (
    .in0(2'b00), .in1(2'b00), .in2(2'b00), .in3(2'b11), .in4(2'b00), .in5(2'b00), .in6(2'b10), .in7(2'b10),
    .out(Reg_Write_Data), .sel({Inst_In[1:0], multiplexer_4_out[0]}));

  assign ALU_Operation = {Inst_In[15:14], Inst_In[7:5], Inst_In[1:0]};
  assign Imm__Encoding = Inst_In[1:0];
endmodule

module Registers (
  input  Clear,
  input  [2:0] rs1_Sele,
  input  [2:0] rs2_Sele,
  input  Clock,
  input  [2:0] rs0_Sele,
  input  Write,
  input  [15:0] Write_Input,
  output [15:0] rs1_Data,
  output [15:0] rs2_Data
);

  wire demultiplexer_1_out1, demultiplexer_1_out2, demultiplexer_1_out3, demultiplexer_1_out4,
       demultiplexer_1_out5, demultiplexer_1_out6, demultiplexer_1_out7;
  wire [15:0] demultiplexer_2_out1, demultiplexer_2_out2, demultiplexer_2_out3, demultiplexer_2_out4,
       demultiplexer_2_out5, demultiplexer_2_out6, demultiplexer_2_out7, x1_q, x2_q, x3_q, x4_q, x5_q, x6_q,
       x7_q;

  Demultiplexer #(.select(3), .enable("false")) demultiplexer_1 (
    .out1(demultiplexer_1_out1), .out2(demultiplexer_1_out2), .out3(demultiplexer_1_out3),
    .out4(demultiplexer_1_out4), .out5(demultiplexer_1_out5), .out6(demultiplexer_1_out6),
    .out7(demultiplexer_1_out7), .in(Write), .sel(rs0_Sele));  // open: out0
  Demultiplexer #(.select(3), .width(16), .enable("false")) demultiplexer_2 (
    .out1(demultiplexer_2_out1), .out2(demultiplexer_2_out2), .out3(demultiplexer_2_out3),
    .out4(demultiplexer_2_out4), .out5(demultiplexer_2_out5), .out6(demultiplexer_2_out6),
    .out7(demultiplexer_2_out7), .in(Write_Input), .sel(rs0_Sele));  // open: out0
  Register #(.width(16)) x1 (.D(demultiplexer_2_out1), .en(demultiplexer_1_out1), .Q(x1_q), .clk(Clock), .clr(Clear));
  Register #(.width(16)) x2 (.D(demultiplexer_2_out2), .en(demultiplexer_1_out2), .Q(x2_q), .clk(Clock), .clr(Clear));
  Register #(.width(16)) x3 (.D(demultiplexer_2_out3), .en(demultiplexer_1_out3), .Q(x3_q), .clk(Clock), .clr(Clear));
  Register #(.width(16)) x4 (.D(demultiplexer_2_out4), .en(demultiplexer_1_out4), .Q(x4_q), .clk(Clock), .clr(Clear));
  Register #(.width(16)) x5 (.D(demultiplexer_2_out5), .en(demultiplexer_1_out5), .Q(x5_q), .clk(Clock), .clr(Clear));
  Register #(.width(16)) x6 (.D(demultiplexer_2_out6), .en(demultiplexer_1_out6), .Q(x6_q), .clk(Clock), .clr(Clear));
  Register #(.width(16)) x7 (.D(demultiplexer_2_out7), .en(demultiplexer_1_out7), .Q(x7_q), .clk(Clock), .clr(Clear));
  Multiplexer #(.select(3), .width(16), .enable("false")) multiplexer_1 (
    .in0({16{1'b0}}), .in1(x1_q), .in2(x2_q), .in3(x3_q), .in4(x4_q), .in5(x5_q), .in6(x6_q), .in7(x7_q),
    .out(rs1_Data), .sel(rs1_Sele));
  Multiplexer #(.select(3), .width(16), .enable("false")) multiplexer_2 (
    .in0({16{1'b0}}), .in1(x1_q), .in2(x2_q), .in3(x3_q), .in4(x4_q), .in5(x5_q), .in6(x6_q), .in7(x7_q),
    .out(rs2_Data), .sel(rs2_Sele));
endmodule

module Imm__Proc (
  input  [13:0] Immediate_Input,
  input  [1:0] Immediate_Encoding,
  output [15:0] Immediate_Output
);

  wire [15:0] bit_extender_1_out, bit_extender_2_out;

  assign bit_extender_1_out = {{11{Immediate_Input[13]}}, Immediate_Input[13:9]};  // Bit_Extender bit_extender_1
  Multiplexer #(.select(2), .width(16), .enable("false")) multiplexer_1 (
    .in1(bit_extender_1_out), .in2(bit_extender_2_out), .in3({Immediate_Input[13:3], {5{1'b0}}}),
    .out(Immediate_Output), .sel(Immediate_Encoding));  // open: in0
  assign bit_extender_2_out = {{11{Immediate_Input[13]}}, {Immediate_Input[13:12], Immediate_Input[2:0]}};  // Bit_Extender bit_extender_2
endmodule

module ALU (
  input  [15:0] IN_1,
  input  [15:0] IN_2,
  input  [6:0] Operation,
  output [15:0] Out
);

  wire [0:0] comparator_1_lt, comparator_2_lt;
  wire [15:0] adder_1_out, adder_2_out, and_1_out, divider_1_out, divider_1_rem, multiplexer_1_out,
       multiplexer_2_out, multiplexer_3_out, multiplexer_4_out, multiplexer_5_out, multiplexer_6_out,
       multiplexer_7_out, multiplexer_8_out, multiplexer_9_out, multiplexer_10_out, multiplexer_11_out,
       multiplexer_12_out, multiplexer_13_out, multiplexer_14_out, multiplexer_15_out, multiplier_1_cout,
       multiplier_1_out, not_1_out, not_2_out, not_3_out, or_1_out, shifter_1_out, shifter_2_out,
       shifter_3_out, subtractor_1_out, xor_1_out;

  Adder #(.width(16)) adder_1 (.a(IN_1), .b(IN_2), .out(adder_1_out));  // open: cin, cout
  Subtractor #(.width(16)) subtractor_1 (.a(IN_1), .b(IN_2), .out(subtractor_1_out));  // open: bin, bout
  Comparator #(.width(16)) comparator_1 (.a(IN_1), .b(IN_2), .lt(comparator_1_lt[0]));  // open: gt, eq
  Comparator #(.width(16), .mode("unsigned")) comparator_2 (
    .a(IN_1), .b(IN_2), .lt(comparator_2_lt[0]));  // open: gt, eq
  Shifter #(.width(16)) shifter_1 (.in(IN_1), .\dist (IN_2[3:0]), .out(shifter_1_out));
  Shifter #(.width(16), .shift("ar")) shifter_2 (.in(IN_1), .\dist (IN_2[3:0]), .out(shifter_2_out));
  Shifter #(.width(16), .shift("lr")) shifter_3 (.in(IN_1), .\dist (IN_2[3:0]), .out(shifter_3_out));
  assign or_1_out = IN_1 | IN_2;  // OR_Gate or_1, 16 bits wide
  assign and_1_out = IN_1 & IN_2;  // AND_Gate and_1, 16 bits wide
  assign xor_1_out = IN_1 ^ IN_2;  // XOR_Gate xor_1, 16 bits wide
  Adder #(.width(16)) adder_2 (.a(IN_1), .b(IN_2), .out(adder_2_out));  // open: cin, cout
  Multiplier #(.width(16)) multiplier_1 (
    .a(IN_1), .b(IN_2), .out(multiplier_1_out), .cout(multiplier_1_cout));  // open: cin
  Divider #(.width(16)) divider_1 (.a(IN_1), .b(IN_2), .out(divider_1_out), .rem(divider_1_rem));  // open: upper
  Multiplexer #(.width(16), .enable("false")) multiplexer_1 (
    .in0(adder_1_out), .in1(subtractor_1_out), .out(multiplexer_1_out), .sel(Operation[5]));
  Multiplexer #(.width(16), .enable("false")) multiplexer_2 (
    .in0({{15{1'b0}}, comparator_1_lt[0]}), .in1({{15{1'b0}}, comparator_2_lt[0]}), .out(multiplexer_2_out),
    .sel(Operation[5]));
  Multiplexer #(.width(16), .enable("false")) multiplexer_3 (
    .in0(shifter_2_out), .in1(shifter_3_out), .out(multiplexer_3_out), .sel(Operation[5]));
  Multiplexer #(.width(16), .enable("false")) multiplexer_4 (
    .in0(or_1_out), .in1(not_1_out), .out(multiplexer_4_out), .sel(Operation[5]));
  assign not_1_out = ~or_1_out;  // NOT_Gate not_1, 16 bits wide
  Multiplexer #(.width(16), .enable("false")) multiplexer_5 (
    .in0(and_1_out), .in1(not_2_out), .out(multiplexer_5_out), .sel(Operation[5]));
  assign not_2_out = ~and_1_out;  // NOT_Gate not_2, 16 bits wide
  Multiplexer #(.width(16), .enable("false")) multiplexer_6 (
    .in0(xor_1_out), .in1(not_3_out), .out(multiplexer_6_out), .sel(Operation[5]));
  assign not_3_out = ~xor_1_out;  // NOT_Gate not_3, 16 bits wide
  Multiplexer #(.select(2), .width(16), .enable("false")) multiplexer_7 (
    .in0(multiplier_1_out), .in1(multiplier_1_cout), .in2(divider_1_out), .in3(divider_1_rem),
    .out(multiplexer_7_out), .sel(Operation[6:5]));
  Multiplexer #(.select(2), .width(16), .enable("false")) multiplexer_8 (
    .in0(multiplexer_1_out), .in1(adder_1_out), .in2(adder_1_out), .out(multiplexer_8_out),
    .sel(Operation[1:0]));  // open: in3
  Multiplexer #(.width(16), .enable("false")) multiplexer_9 (
    .in0(multiplexer_2_out), .in1({{15{1'b0}}, comparator_1_lt[0]}), .out(multiplexer_9_out),
    .sel(Operation[0]));
  Multiplexer #(.width(16), .enable("false")) multiplexer_10 (
    .in0(multiplexer_3_out), .in1(shifter_2_out), .out(multiplexer_10_out), .sel(Operation[0]));
  Multiplexer #(.width(16), .enable("false")) multiplexer_11 (
    .in0(multiplexer_4_out), .in1(or_1_out), .out(multiplexer_11_out), .sel(Operation[0]));
  Multiplexer #(.width(16), .enable("false")) multiplexer_12 (
    .in0(multiplexer_5_out), .in1(and_1_out), .out(multiplexer_12_out), .sel(Operation[0]));
  Multiplexer #(.width(16), .enable("false")) multiplexer_13 (
    .in0(multiplexer_6_out), .in1(xor_1_out), .out(multiplexer_13_out), .sel(Operation[0]));
  Multiplexer #(.width(16), .enable("false")) multiplexer_14 (
    .in0(multiplexer_7_out), .in1(adder_2_out), .out(multiplexer_14_out), .sel(Operation[0]));
  Multiplexer #(.select(3), .width(16), .enable("false")) multiplexer_15 (
    .in0(multiplexer_8_out), .in1(multiplexer_9_out), .in2(shifter_1_out), .in3(multiplexer_10_out),
    .in4(multiplexer_11_out), .in5(multiplexer_12_out), .in6(multiplexer_13_out), .in7(multiplexer_14_out),
    .out(multiplexer_15_out), .sel(Operation[4:2]));
  Multiplexer #(.select(2), .width(16), .enable("false")) multiplexer_16 (
    .in0(multiplexer_15_out), .in1(multiplexer_15_out), .in2(multiplexer_15_out), .in3(IN_2), .out(Out),
    .sel(Operation[1:0]));
endmodule
